# Fritzing sketch MicroPython Rover wiring diagram (saved by Fritzing 0.9.2b)

parts:
  pyboard_v1_1 = PyBoard v1.0  # not connected
  pyboard1 = Micro Python pyboard [part_number=PYBv10b]
  M2 = DC Motor
  Part4 = Bluetooth HC-05
  Part7 = BMP180 Breakout [part_number=SEN-11824]
  M3 = DC Motor
  Part8 = SRF04 Ultrasonic Rangefinder
  PART2 = Motor Driver 1A Dual TB6612FNG [part_number=ROB_09457]
  Part9 = SparkFun 9 Degrees of Freedom Breakout - MPU-9150 [part_number=SEN-11486]
  J1 = Basic Servo
  J2 = Basic Servo

nets:
  GND: pyboard1.P9A_GND, PART2.GND, J2.gnd
  N1: pyboard1.P9B_GND, J1.gnd
  N2: pyboard1.P10A_VIN, J2.vcc
  N3: pyboard1.P10B_VIN, J1.vcc
  N4: pyboard1.X1, J2.pulse
  N5: pyboard1.X2, J1.pulse
  N6: pyboard1.X9, Part7.SCL
  N7: pyboard1.X10, Part7.SDA
  N8: pyboard1.X11, PART2.BIN1
  N9: pyboard1.X12, PART2.BIN2
  GND_2: pyboard1.X14_GND, Part7.GND, Part8.GND
  3.3V: pyboard1.X15_3V3, Part7.3.3V, Part7.IO, Part8.VCC
  N10: pyboard1.Y1, Part4.RXD, Part4.STATE
  N11: pyboard1.Y2, Part4.TXD
  N12: pyboard1.Y3, Part8.TRIG
  N13: pyboard1.Y4, Part8.ECHO
  N14: pyboard1.Y5, PART2.AIN2
  N15: pyboard1.Y6, PART2.AIN1
  N16: pyboard1.Y7, PART2.PWMA
  N17: pyboard1.Y8, PART2.PWMB
  N18: pyboard1.Y9, Part9.SCL
  N19: pyboard1.Y10, Part9.SDA
  GND_3: pyboard1.Y14_GND, Part4.GND, Part9.GND
  VCC: pyboard1.Y15_3V3, Part4.VCC, Part9.VCC
  N20: M2.pin_1, PART2.A02
  N21: M2.pin_2, PART2.A01
  N22: M3.pin_1, PART2.B01
  N23: M3.pin_2, PART2.B02

custom parts:
  BMP180 Breakout: This is a breadboard friendly breakout board for the BMP180 high-precision, temp and pressure sensor.
  SRF04 Ultrasonic Rangefinder: http://www.robot-electronics.co.uk/htm/srf04tech.htm https://www.dfrobot.com/wiki/index.php?title=SRF05_Ultrasonic_sensor_(SKU:SEN0006)
  Motor Driver 1A Dual TB6612FNG: The TB6612FNG motor driver can control up to two DC motors at a constant current of 1.2A (3.2A peak). Two input signals (IN1 and IN2) can be used to control the motor in one of four function modes - CW, CCW, short-brake, and stop. The two motor outputs (A and B) can be separately controlled, the speed of each motor is controlled via a PWM input signal with a frequency up to 100kHz. The STBY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
  SparkFun 9 Degrees of Freedom Breakout - MPU-9150: The SparkFun 9DOF MPU-9150 is the world’s first 9-axis MotionTracking MEMS device designed for the low power, low cost, and high performance requirements of consumer electronics equipment including smartphones, tablets and wearable sensors. And guess what? You get to play with it. This breakout board makes it easy to prototype with the InvenSense MPU-9150 by breaking out all the pins you need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
